# Fritzing sketch Sketch Balanza (saved by Fritzing 0.9.3b)

parts:
  Componente1 = Arduino Pro Mini (3.3V)
  Componente2 = HX711 Weighing Sensor Module
  DS1 = DS18B20 1-Wire Temperature Sensor [part_number=DS18B20]
  R1 = Resistor [tolerance=±5% resistance=4.7k package="2512 [SMD]"]
  U1 = MAX485 [package=dil08]
  J1 = Camdenboss CTB0158-4 [part_number=CTB0158-4 package=THT]

nets:
  VCC: Componente1.VCC, Componente2.VCC, DS1.VDD, R1.Pin_0, U1.VCC, J1.pin1
  N1: Componente1.SCK, U1.RE, U1.DE
  N2: Componente1.D5, Componente2.CK/TX
  N3: Componente1.D4, Componente2.DO/RX
  N4: Componente1.D2, DS1.DQ, R1.Pin_1
  GND: Componente1.GND, Componente2.GND, DS1.GND, U1.GND, J1.pin4
  N5: Componente1.RXI, U1.RO
  N6: Componente1.TXO, U1.DI
  N7: U1.A, J1.pin3
  N8: U1.B, J1.pin2
